// Logisim project riser16.circ as structural Verilog: 1 circuit, main circuit main
module main (
  output out_1,
  output [15:0] out_2,
  output out_3,
  output [15:0] out_4,
  output [15:0] out_5,
  output [15:0] out_6,
  output [15:0] out_7
);

  wire adder_1_cout, and_1_out, clock_1_out, clock_2_out, clock_3_out, clock_4_out, clock_5_out, clock_6_out,
       clock_7_out, clock_8_out, clock_10_out, counter_1_carry, counter_2_carry, nor_1_out, nor_2_out,
       nor_3_out, nor_4_out, nor_5_out, nor_6_out, nor_7_out, nor_8_out, not_1_out, pull_resistor_1_node,
       pull_resistor_2_node, pull_resistor_4_node, pull_resistor_31_node, pull_resistor_32_node,
       pull_resistor_33_node, pull_resistor_36_node, pull_resistor_41_node, pull_resistor_42_node,
       pull_resistor_43_node, pull_resistor_44_node, pull_resistor_45_node, pull_resistor_46_node,
       pull_resistor_49_node, rgb_video_1_p2, subtractor_1_bout;
  wire [2:0] rom_1_data_2;
  wire [3:3] pull_resistor_40_node;
  wire [7:0] pull_resistor_13_node;
  wire [13:0] counter_2_q;
  wire [15:0] adder_1_out, and_2_out, controlled_buffer_1_out, multiplexer_1_out, not_2_out, or_1_out,
       ram_1_dout, register_1_q, register_3_q, shifter_1_out, shifter_2_out, subtractor_1_out, xor_1_out;
  wire [15:8] controlled_buffer_5_out;
  wire [23:0] rom_1_data;

  Clock clock_1 (.out(clock_1_out));
  Register #(.width(16)) register_1 (
    .D(controlled_buffer_1_out), .en(rom_1_data[3]), .clk(clock_2_out), .Q(register_1_q),
    .clr(pull_resistor_1_node));
  Clock clock_2 (.out(clock_2_out));
  RAM #(.addrWidth(16), .dataWidth(16)) ram_1 (
    .addr(register_1_q), .we(rom_1_data[4]), .oe(1'b1), .clk(clock_1_out), .din(controlled_buffer_1_out),
    .dout(ram_1_dout));
  Pull_Resistor pull_resistor_1 (.node(pull_resistor_1_node));
  DotMatrix #(.matrixcols(16), .matrixrows(1)) dotmatrix_1 (
    .col0(register_1_q[15]), .col1(register_1_q[14]), .col2(register_1_q[13]), .col3(register_1_q[12]),
    .col4(register_1_q[11]), .col5(register_1_q[10]), .col6(register_1_q[9]), .col7(register_1_q[8]),
    .col8(register_1_q[7]), .col9(register_1_q[6]), .col10(register_1_q[5]), .col11(register_1_q[4]),
    .col12(register_1_q[3]), .col13(register_1_q[2]), .col14(register_1_q[1]), .col15(register_1_q[0]));
  Counter #(.max('hffff), .width(16)) counter_1 (
    .clr(pull_resistor_2_node), .load(rom_1_data[6]), .up(1'b1), .count(rom_1_data[7]), .clk(clock_3_out),
    .D(controlled_buffer_1_out), .carry(counter_1_carry), .Q(out_5));
  Pull_Resistor pull_resistor_2 (.node(pull_resistor_2_node));
  Clock clock_3 (.out(clock_3_out));
  Pull_Resistor pull_resistor_3 (.node(rom_1_data[9]));
  Pull_Resistor pull_resistor_4 (.node(pull_resistor_4_node));
  Clock clock_4 (.out(clock_4_out));
  Counter #(.max('hf), .width(4)) counter_2 (
    .clr(rom_1_data[9]), .load(pull_resistor_4_node), .up(1'b1), .count(1'b1), .clk(not_1_out),
    .carry(counter_2_carry), .Q(counter_2_q[3:0]));  // open: D
  not not_1 (not_1_out, clock_4_out);
  DotMatrix #(.matrixcols(16), .matrixrows(1)) dotmatrix_2 (
    .col0(counter_2_q[13]), .col1(counter_2_q[12]), .col2(counter_2_q[11]), .col3(counter_2_q[10]),
    .col4(counter_2_q[9]), .col5(counter_2_q[8]), .col6(counter_2_q[7]), .col7(counter_2_q[6]),
    .col8(pull_resistor_13_node[7]), .col9(pull_resistor_13_node[6]), .col10(pull_resistor_13_node[5]),
    .col11(pull_resistor_13_node[4]), .col12(pull_resistor_13_node[3]), .col13(pull_resistor_13_node[2]),
    .col14(pull_resistor_13_node[1]), .col15(pull_resistor_13_node[0]));
  ROM #(.addrWidth(14), .dataWidth(24)) rom_1 (
    .addr(counter_2_q), .data({rom_1_data[23:17], rom_1_data_2, rom_1_data[13:0]}));
  DotMatrix #(.matrixcols(16), .matrixrows(1)) dotmatrix_3 (
    .col0(ram_1_dout[15]), .col1(ram_1_dout[14]), .col2(ram_1_dout[13]), .col3(ram_1_dout[12]),
    .col4(ram_1_dout[11]), .col5(ram_1_dout[10]), .col6(ram_1_dout[9]), .col7(ram_1_dout[8]),
    .col8(ram_1_dout[7]), .col9(ram_1_dout[6]), .col10(ram_1_dout[5]), .col11(ram_1_dout[4]),
    .col12(ram_1_dout[3]), .col13(ram_1_dout[2]), .col14(ram_1_dout[1]), .col15(ram_1_dout[0]));
  assign controlled_buffer_1_out = rom_1_data[5] ? ram_1_dout : 16'bz;  // Controlled_Buffer controlled_buffer_1
  Pull_Resistor pull_resistor_5 (.node(counter_1_carry));
  DotMatrix #(.matrixcols(16), .matrixrows(1)) dotmatrix_4 (
    .col0(out_5[15]), .col1(out_5[14]), .col2(out_5[13]), .col3(out_5[12]), .col4(out_5[11]),
    .col5(out_5[10]), .col6(out_5[9]), .col7(out_5[8]), .col8(out_5[7]), .col9(out_5[6]), .col10(out_5[5]),
    .col11(out_5[4]), .col12(out_5[3]), .col13(out_5[2]), .col14(out_5[1]), .col15(out_5[0]));
  Pull_Resistor pull_resistor_6 (.node(pull_resistor_13_node[7]));
  Pull_Resistor pull_resistor_7 (.node(pull_resistor_13_node[6]));
  Pull_Resistor pull_resistor_8 (.node(pull_resistor_13_node[5]));
  Pull_Resistor pull_resistor_9 (.node(pull_resistor_13_node[4]));
  assign controlled_buffer_1_out = rom_1_data[8] ? out_5 : 16'bz;  // Controlled_Buffer controlled_buffer_2
  DotMatrix #(.matrixcols(4), .matrixrows(1)) dotmatrix_5 (
    .col0(counter_2_q[3]), .col1(counter_2_q[2]), .col2(counter_2_q[1]), .col3(counter_2_q[0]));
  Pull_Resistor pull_resistor_10 (.node(pull_resistor_13_node[3]));
  Pull_Resistor pull_resistor_11 (.node(pull_resistor_13_node[2]));
  Pull_Resistor pull_resistor_12 (.node(pull_resistor_13_node[1]));
  Pull_Resistor pull_resistor_13 (.node(pull_resistor_13_node[0]));
  Pull_Resistor pull_resistor_14 (.node(counter_2_carry));
  DotMatrix #(.matrixcols(4), .matrixrows(1)) dotmatrix_6 (
    .col0(counter_2_q[3]), .col1(counter_2_q[2]), .col2(counter_2_q[1]), .col3(counter_2_q[0]));
  DotMatrix #(.matrixcols(16), .matrixrows(1)) dotmatrix_7 (
    .col0(controlled_buffer_1_out[15]), .col1(controlled_buffer_1_out[14]),
    .col2(controlled_buffer_1_out[13]), .col3(controlled_buffer_1_out[12]),
    .col4(controlled_buffer_1_out[11]), .col5(controlled_buffer_1_out[10]),
    .col6(controlled_buffer_1_out[9]), .col7(controlled_buffer_1_out[8]), .col8(controlled_buffer_1_out[7]),
    .col9(controlled_buffer_1_out[6]), .col10(controlled_buffer_1_out[5]),
    .col11(controlled_buffer_1_out[4]), .col12(controlled_buffer_1_out[3]),
    .col13(controlled_buffer_1_out[2]), .col14(controlled_buffer_1_out[1]), .col15(controlled_buffer_1_out[0]));
  Pull_Resistor pull_resistor_15 (.node(controlled_buffer_1_out[15]));
  Pull_Resistor pull_resistor_16 (.node(controlled_buffer_1_out[14]));
  Pull_Resistor pull_resistor_17 (.node(controlled_buffer_1_out[13]));
  Pull_Resistor pull_resistor_18 (.node(controlled_buffer_1_out[12]));
  Pull_Resistor pull_resistor_19 (.node(controlled_buffer_1_out[11]));
  Pull_Resistor pull_resistor_20 (.node(controlled_buffer_1_out[10]));
  Pull_Resistor pull_resistor_21 (.node(controlled_buffer_1_out[9]));
  Pull_Resistor pull_resistor_22 (.node(controlled_buffer_1_out[8]));
  Pull_Resistor pull_resistor_23 (.node(controlled_buffer_1_out[7]));
  Pull_Resistor pull_resistor_24 (.node(controlled_buffer_1_out[6]));
  Pull_Resistor pull_resistor_25 (.node(controlled_buffer_1_out[5]));
  Pull_Resistor pull_resistor_26 (.node(controlled_buffer_1_out[4]));
  Pull_Resistor pull_resistor_27 (.node(controlled_buffer_1_out[3]));
  Pull_Resistor pull_resistor_28 (.node(controlled_buffer_1_out[2]));
  Pull_Resistor pull_resistor_29 (.node(controlled_buffer_1_out[1]));
  Pull_Resistor pull_resistor_30 (.node(controlled_buffer_1_out[0]));
  DotMatrix #(.matrixcols(8), .matrixrows(1)) dotmatrix_8 (
    .col0(controlled_buffer_5_out[15]), .col1(controlled_buffer_5_out[14]),
    .col2(controlled_buffer_5_out[13]), .col3(controlled_buffer_5_out[12]),
    .col4(controlled_buffer_5_out[11]), .col5(controlled_buffer_5_out[10]),
    .col6(controlled_buffer_5_out[9]), .col7(controlled_buffer_5_out[8]));
  Register #(.width(16)) register_2 (
    .D(controlled_buffer_1_out), .en(rom_1_data[21]), .clk(clock_5_out), .Q(out_2),
    .clr(pull_resistor_31_node));
  Clock clock_5 (.out(clock_5_out));
  Register #(.width(16)) register_3 (
    .D(controlled_buffer_1_out), .en(rom_1_data[12]), .clk(clock_6_out), .Q(register_3_q),
    .clr(pull_resistor_32_node));
  Clock clock_6 (.out(clock_6_out));
  Register #(.width(16)) register_4 (
    .D(controlled_buffer_1_out), .en(rom_1_data[10]), .clk(clock_7_out),
    .Q({counter_2_q[13:6], pull_resistor_13_node}), .clr(pull_resistor_33_node));
  Clock clock_7 (.out(clock_7_out));
  DotMatrix #(.matrixcols(16), .matrixrows(1)) dotmatrix_9 (
    .col0(controlled_buffer_1_out[15]), .col1(controlled_buffer_1_out[14]),
    .col2(controlled_buffer_1_out[13]), .col3(controlled_buffer_1_out[12]),
    .col4(controlled_buffer_1_out[11]), .col5(controlled_buffer_1_out[10]),
    .col6(controlled_buffer_1_out[9]), .col7(controlled_buffer_1_out[8]), .col8(controlled_buffer_1_out[7]),
    .col9(controlled_buffer_1_out[6]), .col10(controlled_buffer_1_out[5]),
    .col11(controlled_buffer_1_out[4]), .col12(controlled_buffer_1_out[3]),
    .col13(controlled_buffer_1_out[2]), .col14(controlled_buffer_1_out[1]), .col15(controlled_buffer_1_out[0]));
  Pull_Resistor pull_resistor_31 (.node(pull_resistor_31_node));
  Pull_Resistor pull_resistor_32 (.node(pull_resistor_32_node));
  Pull_Resistor pull_resistor_33 (.node(pull_resistor_33_node));
  Pull_Resistor pull_resistor_34 (.node(rom_1_data[20]));
  Pull_Resistor pull_resistor_35 (.node(rom_1_data[19]));
  DotMatrix #(.matrixcols(16), .matrixrows(1)) dotmatrix_10 (
    .col0(out_2[15]), .col1(out_2[14]), .col2(out_2[13]), .col3(out_2[12]), .col4(out_2[11]),
    .col5(out_2[10]), .col6(out_2[9]), .col7(out_2[8]), .col8(out_2[7]), .col9(out_2[6]), .col10(out_2[5]),
    .col11(out_2[4]), .col12(out_2[3]), .col13(out_2[2]), .col14(out_2[1]), .col15(out_2[0]));
  assign controlled_buffer_1_out = rom_1_data[22] ? out_2 : 16'bz;  // Controlled_Buffer controlled_buffer_3
  DotMatrix #(.matrixcols(16), .matrixrows(1)) dotmatrix_11 (
    .col0(register_3_q[15]), .col1(register_3_q[14]), .col2(register_3_q[13]), .col3(register_3_q[12]),
    .col4(register_3_q[11]), .col5(register_3_q[10]), .col6(register_3_q[9]), .col7(register_3_q[8]),
    .col8(register_3_q[7]), .col9(register_3_q[6]), .col10(register_3_q[5]), .col11(register_3_q[4]),
    .col12(register_3_q[3]), .col13(register_3_q[2]), .col14(register_3_q[1]), .col15(register_3_q[0]));
  assign controlled_buffer_1_out = rom_1_data[13] ? register_3_q : 16'bz;  // Controlled_Buffer controlled_buffer_4
  DotMatrix #(.matrixcols(16), .matrixrows(1)) dotmatrix_12 (
    .col0(counter_2_q[13]), .col1(counter_2_q[12]), .col2(counter_2_q[11]), .col3(counter_2_q[10]),
    .col4(counter_2_q[9]), .col5(counter_2_q[8]), .col6(counter_2_q[7]), .col7(counter_2_q[6]),
    .col8(pull_resistor_13_node[7]), .col9(pull_resistor_13_node[6]), .col10(pull_resistor_13_node[5]),
    .col11(pull_resistor_13_node[4]), .col12(pull_resistor_13_node[3]), .col13(pull_resistor_13_node[2]),
    .col14(pull_resistor_13_node[1]), .col15(pull_resistor_13_node[0]));
  assign {controlled_buffer_5_out, controlled_buffer_1_out[7:0]} = rom_1_data[11] ? {counter_2_q[13:6], pull_resistor_13_node} : 16'bz;  // Controlled_Buffer controlled_buffer_5
  Clock clock_8 (.out(clock_8_out));
  Register #(.width(16)) register_5 (
    .D(controlled_buffer_1_out), .en(rom_1_data[23]), .clk(clock_8_out), .Q(out_6),
    .clr(pull_resistor_36_node));
  Pull_Resistor pull_resistor_36 (.node(pull_resistor_36_node));
  DotMatrix #(.matrixcols(16), .matrixrows(1)) dotmatrix_13 (
    .col0(controlled_buffer_1_out[15]), .col1(controlled_buffer_1_out[14]),
    .col2(controlled_buffer_1_out[13]), .col3(controlled_buffer_1_out[12]),
    .col4(controlled_buffer_1_out[11]), .col5(controlled_buffer_1_out[10]),
    .col6(controlled_buffer_1_out[9]), .col7(controlled_buffer_1_out[8]), .col8(controlled_buffer_1_out[7]),
    .col9(controlled_buffer_1_out[6]), .col10(controlled_buffer_1_out[5]),
    .col11(controlled_buffer_1_out[4]), .col12(controlled_buffer_1_out[3]),
    .col13(controlled_buffer_1_out[2]), .col14(controlled_buffer_1_out[1]), .col15(controlled_buffer_1_out[0]));
  Pull_Resistor pull_resistor_37 (.node(rom_1_data[2]));
  DotMatrix #(.matrixcols(16), .matrixrows(1)) dotmatrix_14 (
    .col0(multiplexer_1_out[15]), .col1(multiplexer_1_out[14]), .col2(multiplexer_1_out[13]),
    .col3(multiplexer_1_out[12]), .col4(multiplexer_1_out[11]), .col5(multiplexer_1_out[10]),
    .col6(multiplexer_1_out[9]), .col7(multiplexer_1_out[8]), .col8(multiplexer_1_out[7]),
    .col9(multiplexer_1_out[6]), .col10(multiplexer_1_out[5]), .col11(multiplexer_1_out[4]),
    .col12(multiplexer_1_out[3]), .col13(multiplexer_1_out[2]), .col14(multiplexer_1_out[1]),
    .col15(multiplexer_1_out[0]));
  Pull_Resistor pull_resistor_38 (.node(controlled_buffer_1_out[7]));
  assign controlled_buffer_1_out = rom_1_data[17] ? multiplexer_1_out : 16'bz;  // Controlled_Buffer controlled_buffer_6
  Multiplexer #(.select(3), .width(16)) multiplexer_1 (
    .in0(shifter_1_out), .in1(xor_1_out), .in2(or_1_out), .in3(and_2_out), .in4(subtractor_1_out),
    .in5(adder_1_out), .in6(not_2_out), .in7(shifter_2_out), .out(multiplexer_1_out), .sel(rom_1_data_2));
  DotMatrix #(.matrixcols(16), .matrixrows(1)) dotmatrix_15 (
    .col0(out_6[15]), .col1(out_6[14]), .col2(out_6[13]), .col3(out_6[12]), .col4(out_6[11]),
    .col5(out_6[10]), .col6(out_6[9]), .col7(out_6[8]), .col8(out_6[7]), .col9(out_6[6]), .col10(out_6[5]),
    .col11(out_6[4]), .col12(out_6[3]), .col13(out_6[2]), .col14(out_6[1]), .col15(out_6[0]));
  Pull_Resistor pull_resistor_39 (.node(rom_1_data_2[1]));
  Pull_Resistor pull_resistor_40 (.node(pull_resistor_40_node[3]));
  Hex_Digit_Display #(.decimalPoint("false")) hex_digit_display_1 (.value(out_6[15:12]));
  Pull_Resistor pull_resistor_41 (.node(pull_resistor_41_node));
  Pull_Resistor pull_resistor_42 (.node(pull_resistor_42_node));
  Pull_Resistor pull_resistor_43 (.node(pull_resistor_43_node));
  Pull_Resistor pull_resistor_44 (.node(pull_resistor_44_node));
  Pull_Resistor pull_resistor_45 (.node(pull_resistor_45_node));
  Pull_Resistor pull_resistor_46 (.node(pull_resistor_46_node));
  DotMatrix #(.matrixcols(30), .matrixrows(1)) dotmatrix_16 (
    .col0(pull_resistor_41_node), .col1(pull_resistor_42_node), .col2(pull_resistor_43_node),
    .col3(pull_resistor_44_node), .col4(pull_resistor_45_node), .col5(pull_resistor_46_node),
    .col6(rom_1_data[23]), .col7(rom_1_data[22]), .col8(rom_1_data[21]), .col9(rom_1_data[20]),
    .col10(rom_1_data[19]), .col11(rom_1_data[18]), .col12(rom_1_data[17]), .col13(rom_1_data_2[2]),
    .col14(rom_1_data_2[1]), .col15(rom_1_data_2[0]), .col16(rom_1_data[13]), .col17(rom_1_data[12]),
    .col18(rom_1_data[11]), .col19(rom_1_data[10]), .col20(rom_1_data[9]), .col21(rom_1_data[8]),
    .col22(rom_1_data[7]), .col23(rom_1_data[6]), .col24(rom_1_data[5]), .col25(rom_1_data[4]),
    .col26(rom_1_data[3]), .col27(rom_1_data[2]), .col28(rom_1_data[1]), .col29(rom_1_data[0]));
  and and_1 (and_1_out, rom_1_data_2[0], rom_1_data_2[2]);
  Hex_Digit_Display #(.decimalPoint("false")) hex_digit_display_2 (.value(out_6[11:8]));
  Hex_Digit_Display #(.decimalPoint("false")) hex_digit_display_3 (.value(out_6[7:4]));
  Multiplexer multiplexer_2 (.in0(subtractor_1_bout), .in1(adder_1_cout), .out(out_1), .sel(and_1_out));
  Pull_Resistor pull_resistor_47 (.node(register_3_q));
  Pull_Resistor pull_resistor_48 (.node(out_2));
  Hex_Digit_Display #(.decimalPoint("false")) hex_digit_display_4 (.value(out_6[3:0]));
  // RGB_Video #(.cursor("No Cursor"), .scale(8), .width(256)) rgb_video_1: pin names not known; wires that end beside it: rom_1_data[0], rgb_video_1_p2, rom_1_data[1], controlled_buffer_1_out[15:8], controlled_buffer_1_out[6:0], 3'b111
  assign not_2_out = ~out_2;  // NOT_Gate not_2, 16 bits wide
  Adder #(.width(16)) adder_1 (.a(out_2), .b(register_3_q), .out(adder_1_out), .cout(adder_1_cout));  // open: cin
  Subtractor #(.width(16)) subtractor_1 (
    .a(out_2), .b(register_3_q), .out(subtractor_1_out), .bout(subtractor_1_bout));  // open: bin
  assign and_2_out = out_2 & register_3_q;  // AND_Gate and_2, 16 bits wide
  assign or_1_out = out_2 | register_3_q;  // OR_Gate or_1, 16 bits wide
  assign xor_1_out = out_2 ^ register_3_q;  // XOR_Gate xor_1, 16 bits wide
  Shifter #(.width(16)) shifter_1 (.in(out_2), .\dist ({{3{pull_resistor_40_node[3]}}, 1'b1}), .out(shifter_1_out));
  Shifter #(.shift("lr"), .width(16)) shifter_2 (
    .in(out_2), .\dist ({{3{pull_resistor_40_node[3]}}, 1'b1}), .out(shifter_2_out));
  Clock clock_9 (.out(rgb_video_1_p2));
  nor nor_1 (nor_1_out, multiplexer_1_out[0], multiplexer_1_out[1]);
  nor nor_2 (nor_2_out, multiplexer_1_out[2], multiplexer_1_out[3]);
  nor nor_3 (nor_3_out, multiplexer_1_out[4], multiplexer_1_out[5]);
  nor nor_4 (nor_4_out, multiplexer_1_out[6], multiplexer_1_out[7]);
  nor nor_5 (nor_5_out, multiplexer_1_out[8], multiplexer_1_out[9]);
  nor nor_6 (nor_6_out, multiplexer_1_out[10], multiplexer_1_out[11]);
  nor nor_7 (nor_7_out, multiplexer_1_out[12], multiplexer_1_out[13]);
  nor nor_8 (nor_8_out, multiplexer_1_out[14], multiplexer_1_out[15]);
  and and_3 (out_3, nor_1_out, nor_2_out, nor_3_out, nor_4_out, nor_5_out, nor_6_out, nor_7_out, nor_8_out);
  Register #(.width(2)) register_6 (
    .D({out_3, out_1}), .en(rom_1_data[18]), .clk(clock_10_out), .Q(counter_2_q[5:4]),
    .clr(pull_resistor_49_node));
  Clock clock_10 (.out(clock_10_out));
  Pull_Resistor pull_resistor_49 (.node(pull_resistor_49_node));
  DotMatrix #(.matrixcols(2), .matrixrows(1)) dotmatrix_17 (.col0(counter_2_q[5]), .col1(counter_2_q[4]));

  assign out_4 = out_2;
  assign out_7 = out_6;

  // Notes on the sheet:
  //   PC
  //   contents of rom_1 (hex, n*v repeats v):
  //   108 4a0 14*0 108 4a0 14*0 108 4a0 14*0 108 4a0 14*0 108 4a0 3 200 12*0 108 4a0 3 200 12*0 108 4a0 3
  //   200 12*0 108 4a0 3 200 12*0 108 4a0 108 a2 200 11*0 108 4a0 108 a2 200 11*0 108 4a0 108 a2 200 11*0
  //   108 4a0 108 a2 200 11*0 108 4a0 200 13*0 108 4a0 200 13*0 108 4a0 200 13*0 108 4a0 200 13*0 108 4a0
  //   108 60 200 11*0 108 4a0 108 60 200 11*0 108 4a0 108 60 200 11*0 108 4a0 108 60 200 11*0 108 4a0 108
  //   2000a0 200 11*0 108 4a0 108 2000a0 200 11*0 108 4a0 108 2000a0 200 11*0 108 4a0 108 2000a0 200 11*0
  //   108 4a0 108 10a0 200 11*0 108 4a0 108 10a0 200 11*0 108 4a0 108 10a0 200 11*0 108 4a0 108 10a0 200
  //   11*0 108 4a0 274000 200 12*0 108 4a0 274000 200 12*0 108 4a0 274000 200 12*0 108 4a0 274000 200 12*0
  //   108 4a0 c00000 200 12*0 108 4a0 c00000 200 12*0 108 4a0 c00000 200 12*0 108 4a0 c00000 200
  //   Microcorde Cycle
  //   15
  //   0
  //   X
  //   Y
  //   IR
  //   x px
  //   y px
  //   000
  //   001
  //   010
  //   011
  //   100
  //   left shift
  //   xor
  //   or
  //   and
  //   subtract
  //   101
  //   add
  //   110
  //   not
  //   111
  //   right shift
  //   out src 1
  //   0
  //   1
  //   2
  //   3
  //   out src 2
endmodule
